// Logisim project lab_4bit_adder_sub.circ as structural Verilog: 1 circuit, main circuit main
module main (
  input  C,
  input  [3:0] in_2,
  input  [3:0] in_3,
  input  in_4,
  input  in_5,
  input  in_6
);

  wire and_1_out, and_2_out, and_3_out, and_4_out, and_5_out, and_6_out, and_7_out, and_8_out, or_1_out,
       or_2_out, or_3_out, X0_out, X1_out, X2_out, X3_out, xor_1_out, xor_3_out, xor_5_out, xor_7_out;
  wire [0:0] or_4_out;
  wire [3:0] xor_2_out;

  Hex_Digit_Display hex_digit_display_1 (.value({in_6, in_5, in_4, or_4_out[0]}));  // open: dp
  Hex_Digit_Display hex_digit_display_2 (.value(xor_2_out));  // open: dp
  Hex_Digit_Display hex_digit_display_3 (.value(in_2));  // open: dp
  Hex_Digit_Display hex_digit_display_4 (.value(in_3));  // open: dp
  xor X0 (X0_out, in_2[0], C);
  xor X1 (X1_out, in_2[1], C);
  xor X2 (X2_out, in_2[2], C);
  xor X3 (X3_out, in_2[3], C);
  xor xor_1 (xor_1_out, C, X0_out);
  and and_1 (and_1_out, C, X0_out);
  xor xor_2 (xor_2_out[0], xor_1_out, in_3[0]);
  and and_2 (and_2_out, xor_1_out, in_3[0]);
  or or_1 (or_1_out, and_2_out, and_1_out);
  xor xor_3 (xor_3_out, or_1_out, X1_out);
  and and_3 (and_3_out, or_1_out, X1_out);
  xor xor_4 (xor_2_out[1], xor_3_out, in_3[1]);
  and and_4 (and_4_out, xor_3_out, in_3[1]);
  or or_2 (or_2_out, and_4_out, and_3_out);
  xor xor_5 (xor_5_out, or_2_out, X2_out);
  and and_5 (and_5_out, or_2_out, X2_out);
  xor xor_6 (xor_2_out[2], xor_5_out, in_3[2]);
  and and_6 (and_6_out, xor_5_out, in_3[2]);
  xor xor_7 (xor_7_out, or_3_out, X3_out);
  and and_7 (and_7_out, or_3_out, X3_out);
  or or_3 (or_3_out, and_6_out, and_5_out);
  and and_8 (and_8_out, xor_7_out, in_3[3]);
  xor xor_8 (xor_2_out[3], xor_7_out, in_3[3]);
  or or_4 (or_4_out[0], and_8_out, and_7_out);

  // Notes on the sheet:
  //   CARRY/BORROW
  //   X+Y
  //   Y-X
  //   X
  //   Y
  //   SUM/DIFF
endmodule
