// Logisim project lab_COUNTLOOPS.circ as structural Verilog: 1 circuit, main circuit main
module main (
  input  in_1,
  input  in_2,
  input  SET,
  input  RESET,
  input  SET_2,
  input  in_6,
  input  STOPWATCH,
  input  SET_3,
  input  in_9,
  input  in_10,
  input  in_11,
  input  in_12,
  input  in_13,
  input  SET_4,
  input  in_15,
  input  in_16,
  input  in_17,
  input  in_18,
  input  in_19,
  input  RST,
  input  RES,
  input  in_22
);

  wire adder_1_cout, and_1_out, and_2_out, and_3_out, and_4_out, and_5_out, and_6_out, and_7_out, and_8_out,
       and_9_out, and_10_out, and_11_out, and_12_out, and_13_out, and_14_out, clock_1_out, clock_2_out,
       clock_3_out, clock_4_out, clock_5_out, clock_6_out, not_1_out, not_2_out, not_3_out, or_1_out,
       t_ff_2_q, t_ff_4_q, t_ff_5_q, t_ff_6_q;
  wire [1:0] t_ff_11_q;
  wire [2:0] t_ff_4_qn, t_ff_6_qn;
  wire [3:0] adder_1_out, d_ff_4_q, t_ff_13_q, t_ff_18_q, t_ff_20_q;

  and and_1 (and_1_out, t_ff_4_q, t_ff_2_q);
  T_Flip_Flop t_ff_1 (.T(and_1_out), .clk(clock_1_out), .Qn(t_ff_4_qn[2]), .reset(RESET), .preset(SET));  // open: Q
  Clock clock_1 (.out(clock_1_out));
  T_Flip_Flop t_ff_2 (.T(t_ff_4_q), .clk(clock_1_out), .Q(t_ff_2_q), .Qn(t_ff_4_qn[1]), .reset(RESET), .preset(SET));
  and and_2 (and_2_out, t_ff_6_q, t_ff_5_q);
  T_Flip_Flop t_ff_3 (.T(and_2_out), .clk(clock_2_out), .Qn(t_ff_6_qn[2]), .reset(in_13), .preset(in_12));  // open: Q
  Clock clock_2 (.out(clock_2_out));
  T_Flip_Flop t_ff_4 (.T(in_2), .clk(clock_1_out), .Q(t_ff_4_q), .Qn(t_ff_4_qn[0]), .reset(RESET), .preset(SET));
  not not_1 (not_1_out, t_ff_6_qn[2]);
  not not_2 (not_2_out, t_ff_6_qn[1]);
  not not_3 (not_3_out, t_ff_6_qn[0]);
  T_Flip_Flop t_ff_5 (.T(t_ff_6_q), .clk(clock_2_out), .Q(t_ff_5_q), .Qn(t_ff_6_qn[1]), .reset(in_13), .preset(in_12));
  and and_3 (and_3_out, t_ff_4_qn[2], t_ff_4_qn[1], t_ff_4_qn[0]);
  T_Flip_Flop t_ff_6 (.T(in_11), .clk(clock_2_out), .Q(t_ff_6_q), .Qn(t_ff_6_qn[0]), .reset(in_13), .preset(in_12));
  T_Flip_Flop t_ff_7 (.T(and_9_out), .clk(clock_4_out), .Q(t_ff_13_q[3]), .reset(in_9), .preset(SET_3));  // open: Qn
  and and_4 (and_4_out, not_1_out, not_2_out, not_3_out);
  and and_5 (and_5_out, t_ff_6_qn[2], not_2_out, not_3_out);
  T_Flip_Flop t_ff_8 (.T(t_ff_11_q[0]), .clk(clock_3_out), .Q(t_ff_11_q[1]), .reset(RST), .preset(in_19));  // open: Qn
  Clock clock_3 (.out(clock_3_out));
  Hex_Digit_Display #(.decimalPoint("false")) hex_digit_display_1 (.value({in_1, t_ff_4_qn}));
  T_Flip_Flop t_ff_9 (.T(and_7_out), .clk(clock_4_out), .Q(t_ff_13_q[2]), .reset(in_9), .preset(SET_3));  // open: Qn
  or or_1 (or_1_out, and_4_out, and_5_out);
  and and_6 (and_6_out, STOPWATCH, t_ff_13_q[0]);
  T_Flip_Flop t_ff_10 (.T(and_6_out), .clk(clock_4_out), .Q(t_ff_13_q[1]), .reset(in_9), .preset(SET_3));  // open: Qn
  Clock clock_4 (.out(clock_4_out));
  Hex_Digit_Display #(.decimalPoint("false")) hex_digit_display_2 (.value({in_10, t_ff_6_qn}));
  T_Flip_Flop t_ff_11 (.T(in_18), .clk(clock_3_out), .Q(t_ff_11_q[0]), .reset(RST), .preset(in_19));  // open: Qn
  T_Flip_Flop t_ff_12 (.T(and_12_out), .clk(clock_5_out), .Q(t_ff_18_q[3]), .reset(in_6), .preset(SET_2));  // open: Qn
  and and_7 (and_7_out, and_6_out, t_ff_13_q[1]);
  T_Flip_Flop t_ff_13 (.T(STOPWATCH), .clk(clock_4_out), .Q(t_ff_13_q[0]), .reset(in_9), .preset(SET_3));  // open: Qn
  T_Flip_Flop t_ff_14 (.T(and_11_out), .clk(clock_5_out), .Q(t_ff_18_q[2]), .reset(in_6), .preset(SET_2));  // open: Qn
  Clock clock_5 (.out(clock_5_out));
  T_Flip_Flop t_ff_15 (.T(and_14_out), .clk(clock_6_out), .Q(t_ff_20_q[3]), .reset(in_15), .preset(SET_4));  // open: Qn
  Hex_Digit_Display #(.decimalPoint("false")) hex_digit_display_3 (.value({{2{in_17}}, t_ff_11_q}));
  and and_8 (and_8_out, and_3_out, t_ff_18_q[0]);
  T_Flip_Flop t_ff_16 (.T(and_8_out), .clk(clock_5_out), .Q(t_ff_18_q[1]), .reset(in_6), .preset(SET_2));  // open: Qn
  Hex_Digit_Display #(.decimalPoint("false")) hex_digit_display_4 (.value(t_ff_13_q));
  and and_9 (and_9_out, t_ff_13_q[2], and_7_out);
  T_Flip_Flop t_ff_17 (.T(and_13_out), .clk(clock_6_out), .Q(t_ff_20_q[2]), .reset(in_15), .preset(SET_4));  // open: Qn
  Clock clock_6 (.out(clock_6_out));
  T_Flip_Flop t_ff_18 (.T(and_3_out), .clk(clock_5_out), .Q(t_ff_18_q[0]), .reset(in_6), .preset(SET_2));  // open: Qn
  and and_10 (and_10_out, or_1_out, t_ff_20_q[0]);
  T_Flip_Flop t_ff_19 (.T(and_10_out), .clk(clock_6_out), .Q(t_ff_20_q[1]), .reset(in_15), .preset(SET_4));  // open: Qn
  D_Flip_Flop d_ff_1 (.D(adder_1_out[3]), .clk(clock_3_out), .Q(d_ff_4_q[3]), .preset(in_22), .reset(RES));  // open: Qn
  and and_11 (and_11_out, and_8_out, t_ff_18_q[1]);
  T_Flip_Flop t_ff_20 (.T(or_1_out), .clk(clock_6_out), .Q(t_ff_20_q[0]), .reset(in_15), .preset(SET_4));  // open: Qn
  D_Flip_Flop d_ff_2 (.D(adder_1_out[2]), .clk(clock_3_out), .Q(d_ff_4_q[2]), .preset(in_22), .reset(RES));  // open: Qn
  Hex_Digit_Display #(.decimalPoint("false")) hex_digit_display_5 (.value(t_ff_18_q));
  and and_12 (and_12_out, t_ff_18_q[2], and_11_out);
  and and_13 (and_13_out, and_10_out, t_ff_20_q[1]);
  D_Flip_Flop d_ff_3 (.D(adder_1_out[1]), .clk(clock_3_out), .Q(d_ff_4_q[1]), .preset(in_22), .reset(RES));  // open: Qn
  Hex_Digit_Display #(.decimalPoint("false")) hex_digit_display_6 (.value(t_ff_20_q));
  and and_14 (and_14_out, t_ff_20_q[2], and_13_out);
  Adder #(.width(4)) adder_1 (
    .a({{2{in_17}}, t_ff_11_q}), .b(d_ff_4_q), .out(adder_1_out), .cin(in_16), .cout(adder_1_cout));
  D_Flip_Flop d_ff_4 (.D(adder_1_out[0]), .clk(clock_3_out), .Q(d_ff_4_q[0]), .preset(in_22), .reset(RES));  // open: Qn
  Hex_Digit_Display #(.decimalPoint("false")) hex_digit_display_7 (.value(adder_1_out));

  // Notes on the sheet:
  //   Q1)
  //   Q3)
  //   Q4)
  //   Q2)
  //   RESET
  //   RESET
  //   RESET
endmodule
