// Logisim project lab_encoder_2bit_mag_comparator.circ as structural Verilog: 2 circuits, main circuit main
module main (
  input  A0,
  input  A1,
  input  A2,
  input  A3,
  input  B0,
  input  B1,
  input  B2,
  input  B3
);

  wire mag_comp_1_e, mag_comp_1_g, mag_comp_1_l, or_1_out, or_2_out, or_3_out, or_4_out;

  or or_1 (or_1_out, A1, A3);
  or or_2 (or_2_out, A2, A3);
  or or_3 (or_3_out, B1, B3);
  or or_4 (or_4_out, B2, B3);
  mag_comp mag_comp_1 (
    .B0(or_3_out), .A1(or_2_out), .A0(or_1_out), .B1(or_4_out), .e(mag_comp_1_e), .g(mag_comp_1_g),
    .l(mag_comp_1_l));
  LED led_1 (.in(mag_comp_1_e));
  LED led_2 (.in(mag_comp_1_g));
  LED led_3 (.in(mag_comp_1_l));

  // Notes on the sheet:
  //   0
  //   1
  //   2
  //   3
  //   0
  //   1
  //   2
  //   3
  //   A1
  //   B1
  //   A0
  //   B0
  //   A=B
  //   A>B
  //   A<B
endmodule

module mag_comp (
  input  B0,
  input  A1,
  input  A0,
  input  B1,
  output e,
  output g,
  output l
);

  wire and_1_out, and_2_out, and_3_out, and_4_out, and_5_out, and_6_out, not_1_out, not_2_out, not_3_out,
       not_4_out, xnor_1_out, xnor_2_out;

  not not_1 (not_1_out, A1);
  not not_2 (not_2_out, A0);
  not not_3 (not_3_out, B1);
  not not_4 (not_4_out, B0);
  xnor xnor_1 (xnor_1_out, A1, B1);
  xnor xnor_2 (xnor_2_out, A0, B0);
  and and_1 (and_1_out, A0, not_4_out);
  and and_2 (and_2_out, A1, not_3_out);
  and and_3 (and_3_out, not_1_out, B1);
  and and_4 (and_4_out, B0, not_2_out);
  and and_5 (and_5_out, xnor_1_out, and_1_out);
  and and_6 (and_6_out, xnor_1_out, and_4_out);
  or or_1 (g, and_5_out, and_2_out);
  or or_2 (l, and_3_out, and_6_out);
  and and_7 (e, xnor_1_out, xnor_2_out);
endmodule
