// Logisim project lab_gates_base.circ as structural Verilog: 1 circuit, main circuit main
module main (
  input  A,
  input  B,
  input  c,
  input  a_2,
  input  B_2,
  input  A_3,
  input  B_3,
  input  C_2,
  input  A_4,
  input  B_4,
  input  C_3,
  input  D
);

  wire and_1_out, and_2_out, and_3_out, and_4_out, and_5_out, and_6_out, and_7_out, and_8_out, and_9_out,
       and_10_out, and_11_out, and_12_out, and_13_out, and_14_out, and_15_out, and_16_out, and_17_out,
       and_18_out, and_19_out, and_20_out, and_21_out, and_22_out, not_1_out, not_2_out, not_3_out,
       not_4_out, not_5_out, not_6_out, not_7_out, not_8_out, not_9_out, not_10_out, or_1_out, or_2_out,
       or_3_out, or_4_out, or_5_out, or_6_out, or_7_out, or_8_out, or_9_out, or_10_out, or_11_out;

  not not_1 (not_1_out, B);
  not not_2 (not_2_out, c);
  and and_1 (and_1_out, A, not_1_out);
  and and_2 (and_2_out, B, not_2_out);
  and and_3 (and_3_out, not_2_out, A);
  not not_3 (not_3_out, a_2);
  not not_4 (not_4_out, B_2);
  not not_5 (not_5_out, A_3);
  not not_6 (not_6_out, A_4);
  not not_7 (not_7_out, B_4);
  not not_8 (not_8_out, C_3);
  not not_9 (not_9_out, B_3);
  not not_10 (not_10_out, C_2);
  and and_4 (and_4_out, not_8_out, D);
  or or_1 (or_1_out, and_1_out, and_2_out);
  and and_5 (and_5_out, not_3_out, B_2);
  and and_6 (and_6_out, a_2, not_4_out);
  and and_7 (and_7_out, not_4_out, not_3_out);
  and and_8 (and_8_out, not_5_out, not_9_out);
  and and_9 (and_9_out, B_3, A_3);
  and and_10 (and_10_out, A_4, B_4);
  and and_11 (and_11_out, B_4, C_3);
  and and_12 (and_12_out, not_6_out, not_7_out);
  LED led_1 (.in(or_2_out));
  or or_2 (or_2_out, or_1_out, and_3_out);
  and and_13 (and_13_out, and_11_out, D);
  and and_14 (and_14_out, and_10_out, D);
  and and_15 (and_15_out, and_12_out, and_4_out);
  or or_3 (or_3_out, and_5_out, and_6_out);
  and and_16 (and_16_out, not_5_out, B_3);
  and and_17 (and_17_out, and_8_out, C_2);
  and and_18 (and_18_out, and_8_out, not_10_out);
  and and_19 (and_19_out, not_10_out, and_9_out);
  and and_20 (and_20_out, not_8_out, and_10_out);
  and and_21 (and_21_out, and_13_out, A_4);
  or or_4 (or_4_out, and_14_out, and_15_out);
  or or_5 (or_5_out, or_3_out, and_7_out);
  and and_22 (and_22_out, and_16_out, not_10_out);
  or or_6 (or_6_out, and_18_out, and_19_out);
  or or_7 (or_7_out, and_20_out, and_13_out);
  or or_8 (or_8_out, and_21_out, or_4_out);
  LED led_2 (.in(or_5_out));
  or or_9 (or_9_out, and_22_out, and_17_out);
  or or_10 (or_10_out, or_7_out, or_8_out);
  LED led_3 (.in(or_11_out));
  or or_11 (or_11_out, or_9_out, or_6_out);
  LED led_4 (.in(or_10_out));

  // Notes on the sheet:
  //   2)
  //   1)
  //   3)
  //   4)
  //   AB'
  //   BC'
  //   AC'
  //   a'b
  //   ab'
  //   A'B'
  //   A'B''
  //   AB
  //   BCD
  //   ABD
  //   A'B'C'D
  //   A'B'C
  //   A'B'C'
  //   A'B
  //   A'BC'
  //   ABC'
  //   ABC'
  //   ABCD
endmodule
